# Fritzing sketch Analog_IO (saved by Fritzing 0.9.1b)
breadboards: 1

parts:
  Part1 = Arduino Uno (Rev3)
  R1 = Resistor [tolerance=±5% resistance=220 package=THT]
  R4 = Resistor [tolerance=±5% resistance=220 package=THT]
  LED1 = LED - 5mm [color="Red (633nm)" package="5 mm [THT]"]
  R5 = Resistor [tolerance=±5% resistance=220 package=THT]

nets:
  N1: Part1.A0, R1.Pin_1, R4.Pin_0
  N2: Part1.D9_PWM, LED1.cathode
  N3: Part1.GND, R4.Pin_1, R5.Pin_0
  N4: Part1.5V, R1.Pin_0
  N5: LED1.anode, R5.Pin_1
