# Fritzing sketch blink-button (saved by Fritzing 0.9.2b)
breadboards: 1

parts:
  LED1 = LED - 5mm [color="Red (633nm)" package="5 mm [THT]"]
  R1 = Resistor [tolerance=±5% resistance=1k package="0402 [SMD]"]
  Part1 = Arduino Uno (Rev3)
  S1 = Pushbutton [package="[THT]"]
  R2 = Resistor [tolerance=±5% resistance=10k package="0402 [SMD]"]

nets:
  N1: LED1.cathode, R1.Pin_1
  N2: LED1.anode, Part1.GND, R2.Pin_1
  N3: R1.Pin_0, Part1.D7
  N4: Part1.D2, S1.Pin_1, S1.Pin_2, R2.Pin_0
  N5: Part1.5V, S1.Pin_3, S1.Pin_4
